// Logisim project Prac_4_1.circ as structural Verilog: 1 circuit, main circuit main
module main (
  input  P3,
  input  G3,
  input  P2,
  input  G2,
  input  P1,
  input  G1,
  input  P0,
  input  G0,
  input  C0,
  output C4,
  output C3,
  output C2,
  output C1
);

  wire and_1_out, and_2_out, and_3_out, and_4_out, and_5_out, and_6_out, and_7_out, and_8_out, and_9_out,
       and_10_out;

  and and_1 (and_1_out, P3, P2, P1, P0, C0);
  and and_2 (and_2_out, P3, P2, P1, G0);
  and and_3 (and_3_out, P3, P2, G1);
  and and_4 (and_4_out, P3, G2);
  and and_5 (and_5_out, P2, P1, P0, C0);
  and and_6 (and_6_out, P2, P1, G0);
  and and_7 (and_7_out, P2, G1);
  and and_8 (and_8_out, P0, P1, C0);
  and and_9 (and_9_out, P1, G0);
  and and_10 (and_10_out, P0, C0);
  or or_1 (C4, and_1_out, and_2_out, and_3_out, and_4_out, G3);
  or or_2 (C3, and_5_out, and_6_out, and_7_out, G2);
  or or_3 (C2, and_8_out, and_9_out, G1);
  or or_4 (C1, and_10_out, G0);

  // Notes on the sheet:
  //   Anik Shaikh
  //   Sem 2
  //   Batch - 24
  //   Enrollment no. 23162121021
  //   Look ahead carry generator
endmodule
