// Logisim project Prac_4_1_IC.circ as structural Verilog: 1 circuit, main circuit main
module main (
  input  A0,
  input  Cin,
  input  B0,
  input  A1,
  input  B1,
  input  A2,
  input  B2,
  input  A3,
  input  B3,
  output S0,
  output S1,
  output S2,
  output S3,
  output S4
);

  wire and_1_out, and_2_out, and_3_out, and_4_out, main_1_c1, main_1_c2, main_1_c3, xor_1_out, xor_2_out,
       xor_3_out, xor_4_out;

  xor xor_1 (xor_1_out, A3, B3);
  and and_1 (and_1_out, A3, B3);
  xor xor_2 (xor_2_out, A0, B0);
  and and_2 (and_2_out, A0, B0);
  xor xor_3 (xor_3_out, A1, B1);
  and and_3 (and_3_out, A1, B1);
  xor xor_4 (xor_4_out, A2, B2);
  and and_4 (and_4_out, A2, B2);
  Prac_4_1_main main_1 (
    .P3(xor_1_out), .G3(and_1_out), .P2(xor_4_out), .G2(and_4_out), .P1(xor_3_out), .G1(and_3_out),
    .P0(xor_2_out), .G0(and_2_out), .C0(Cin), .C4(S4), .C3(main_1_c3), .C2(main_1_c2), .C1(main_1_c1));
  xor xor_5 (S0, Cin, xor_2_out);
  xor xor_6 (S1, xor_3_out, main_1_c1);
  xor xor_7 (S2, xor_4_out, main_1_c2);
  xor xor_8 (S3, xor_1_out, main_1_c3);

  // Notes on the sheet:
  //   Anik Shaikh
  //   Sem 2
  //   Batch - 24
  //   Enrollment no. 23162121021
  //   Carry look ahead adder
endmodule
